# Fritzing sketch control_galpon (saved by Fritzing 0.9.2b)
breadboards: 1

parts:
  Parte1 = Arduino Uno (Rev3)
  U1 = 2.4GHz Low Power Transceiver [package=qfn20]
  Tiny_RTC1 = Tiny RTC

nets:
  N1: Parte1.D9_PWM, U1.CE
  N2: Parte1.D10_PWM/SS, U1.CSN
  N3: Parte1.D11_PWM/MOSI, U1.MOSI
  N4: Parte1.D12/MISO, U1.MISO
  N5: Parte1.D13/SCK, U1.SCK
  N6: Parte1.A4/SDA, Tiny_RTC1.SDA
  N7: Parte1.A5/SCL, Tiny_RTC1.SCL
  N8: Parte1.D2, Tiny_RTC1.SQ
  N9: Parte1.D3_PWM, Tiny_RTC1.DS
  3V3: Parte1.3V3, U1.VDD
  5V: Parte1.5V, Tiny_RTC1.VCC
  GND: U1.VSS, Tiny_RTC1.GND

custom parts:
  Tiny RTC: Tiny RTC I2C module DS1370Z RTC and AT24C32 EEPROM
